// Digital circuit dffOpt.dig as structural Verilog
module dffOpt (
  input  D,
  input  C,
  output Q,
  output Q_2
);

  wire nfet_1_s, nfet_4_s, RESET, RESET_t, SET, SET_t;

  PullUp pullup_1 (.out(RESET_t));
  NFET nfet_1 (.G(D), .D(RESET_t), .S(nfet_1_s));
  NFET nfet_2 (.G(Q), .D(Q_2), .S(nfet_1_s));
  NFET nfet_3 (.G(RESET), .D(nfet_1_s), .S(1'b0));
  PullUp pullup_2 (.out(Q_2));
  \nand  nand_1 (.In_1(SET), .In_2(C), .Out(SET_t));
  PullUp pullup_3 (.out(RESET));
  s2 s2_1 (._1(RESET_t), ._2(C), .D(RESET), .S(nfet_4_s));
  PullUp pullup_4 (.out(SET));
  NFET nfet_4 (.G(RESET_t), .D(SET), .S(nfet_4_s));
  NFET nfet_5 (.G(SET_t), .D(nfet_4_s), .S(1'b0));
  PullUp pullup_5 (.out(Q));
  NFET nfet_6 (.G(Q_2), .D(Q), .S(nfet_4_s));

  // Other names for the same wires on the sheet: Q_t = Q_2
endmodule
