// Digital circuit dffRopt.dig as structural Verilog
module dffRopt (
  input  R,
  input  D,
  input  C,
  output Q,
  output Q_2
);

  wire nfet_1_s, nfet_2_s, nfet_4_s, nfet_7_s, RESET, S_1, S_2, SET;

  PullUp pullup_1 (.out(SET));
  NFET nfet_1 (.G(S_2), .D(SET), .S(nfet_1_s));
  NFET nfet_2 (.G(C), .D(nfet_1_s), .S(nfet_2_s));
  NFET nfet_3 (.G(R), .D(nfet_2_s), .S(1'b0));
  NFET nfet_4 (.G(D), .D(S_1), .S(nfet_4_s));
  NFET nfet_5 (.G(RESET), .D(nfet_4_s), .S(nfet_2_s));
  PullUp pullup_2 (.out(S_1));
  PullUp pullup_3 (.out(Q_2));
  NFET nfet_6 (.G(Q), .D(Q_2), .S(nfet_4_s));
  PullUp pullup_4 (.out(S_2));
  NFET nfet_7 (.G(S_1), .D(S_2), .S(nfet_7_s));
  NFET nfet_8 (.G(SET), .D(nfet_7_s), .S(1'b0));
  PullUp pullup_5 (.out(Q));
  NFET nfet_9 (.G(Q_2), .D(Q), .S(nfet_7_s));
  NFET nfet_10 (.G(C), .D(RESET), .S(S_2));
  PullUp pullup_6 (.out(RESET));

  // Other names for the same wires on the sheet: Q_t = Q_2

  // Notes on the sheet:
  //   R: default 1
endmodule
