// Digital circuit tffD.dig as structural Verilog
module tffD (
  input  T,
  input  E,
  input  D,
  output Q,
  output Q_2
);

  wire D_t;

  dffAen dffaen_1 (.D(Q_2), .C(T), .E(E), .Q(Q), .Q_2(Q_2), .R(D_t), .S(D));
  \not  not_1 (.In(D), .Out(D_t));
endmodule
