// Digital circuit d.dig as structural Verilog
module d (
  input  D,
  input  E,
  output Q,
  output Q_2
);

  wire nand_1_out, nand_2_out;

  \nand  nand_1 (.In_1(D), .In_2(E), .Out(nand_1_out));
  \nand  nand_2 (.In_1(nand_1_out), .In_2(E), .Out(nand_2_out));
  sr sr_1 (.S(nand_1_out), .R(nand_2_out), .Out(Q), .Out_2(Q_2));
endmodule
