// Digital circuit computer_toy.dig as structural Verilog
module computer_toy (
  input  Load_ACC,
  input  Load_H,
  input  In_0,
  input  In_1,
  input  In_2,
  input  In_3,
  input  In_4,
  input  In_5,
  input  In_6,
  input  In_7,
  input  Load_In,
  input  Load_M,
  input  Load_L,
  input  Carry_In,
  input  nx,
  input  ny,
  input  f,
  input  no,
  input  Load_ROM,
  input  clk,
  input  Run,
  output [7:0] ALU,
  output [7:0] D,
  output [7:0] ACC,
  output [7:0] H,
  output [7:0] In,
  output [7:0] M,
  output [7:0] L,
  output [15:0] A,
  output [15:0] PC,
  output [7:0] ROM,
  output [7:0] PC_H,
  output [7:0] PC_L,
  output [7:0] Bus
);

  wire and_1_out, clk_e, clk_s, clk_t, Inc__PC_out, nm_alu_fet80_1_c_out, nm_conditionals_1_eqz,
       nm_conditionals_1_gez, nm_conditionals_1_gtz, nm_conditionals_1_lez, nm_conditionals_1_ltz,
       nm_conditionals_1_nez, nm_conditionals_prestage_1_ng, nm_conditionals_prestage_1_zr, nm_or_1_out,
       nm_or_2_out, nm_or_3_out, nm_or_4_out, nm_or_5_out, nm_or_6_out, nm_or_7_out, Save_ACC_out, Set_D_out,
       Set_H_out, Set_L_out, Set_M_out, set_master, Set_PC_H_out, Set_PC_L_out, Set_PC_out, zero_bus;

  Button Inc__PC (.out(Inc__PC_out));
  nm_or nm_or_1 (.Out(nm_or_1_out), .In_1(set_master), .In_2(Set_PC_H_out));
  Button Set_PC_H (.out(Set_PC_H_out));
  nm_or nm_or_2 (.Out(nm_or_2_out), .In_1(set_master), .In_2(Set_PC_L_out));
  Button Set_PC_L (.out(Set_PC_L_out));
  nm_or nm_or_3 (.Out(nm_or_3_out), .In_1(set_master), .In_2(Set_PC_out));
  Button Set_PC (.out(Set_PC_out));
  nm_enableoc8 nm_enableoc8_1 (.In({In_7, In_6, In_5, In_4, In_3, In_2, In_1, In_0}), .en(Load_In), .Out(Bus));
  nm_byte_latch nm_byte_latch_1 (.D(Bus), .set(nm_or_1_out), .Out(PC_H));  // open: Out_2
  nm_byte_latch nm_byte_latch_2 (.D(Bus), .set(nm_or_2_out), .Out(PC_L));  // open: Out_2
  nm_zerooc8 nm_zerooc8_1 (.Bus(Bus), .zero(zero_bus));
  and and_1 (and_1_out, clk, Run);
  PullUp #(.Bits(8)) pullup_1 (.out(Bus));
  nm_clock_gen nm_clock_gen_1 (.clk_e(clk_e), .clk_s(clk_s), .clk_o(clk_t), .clk_i(and_1_out), .r(Run));
  nm_counter16_pc nm_counter16_pc_1 (
    .clk(Inc__PC_out), .D({PC_H, PC_L}), .D_load(nm_or_3_out), .Out(PC));  // open: clk_out
  ROM #(.AddrBits(16), .Bits(8)) rom_1 (.A(PC), .sel(1'b1), .D(ROM));
  Button Set_D (.out(Set_D_out));
  nm_startup nm_startup_1 (.r(Run), .zero_bus(zero_bus), .set_master(set_master), .clk_e(clk_e), .clk_s(clk_s));
  nm_enableoc8 nm_enableoc8_2 (.In(ROM), .en(Load_ROM), .Out(Bus));
  nm_or nm_or_4 (.Out(nm_or_4_out), .In_1(set_master), .In_2(Set_D_out));
  nm_byte_latch nm_byte_latch_3 (.D(Bus), .set(nm_or_4_out), .Out(D));  // open: Out_2
  nm_ALU_FET80 nm_alu_fet80_1 (
    .X(Bus), .Y(D), .c_in(Carry_In), .Out(ALU), .c_out(nm_alu_fet80_1_c_out), .nx(nx), .ny(ny), .f(f), .no(no));
  nm_or nm_or_5 (.Out(nm_or_5_out), .In_1(set_master), .In_2(Set_H_out));
  Button Set_H (.out(Set_H_out));
  nm_or nm_or_6 (.Out(nm_or_6_out), .In_1(set_master), .In_2(Set_L_out));
  Button Set_L (.out(Set_L_out));
  nm_conditionals_prestage nm_conditionals_prestage_1 (
    .zr(nm_conditionals_prestage_1_zr), .ng(nm_conditionals_prestage_1_ng), .In(ALU));
  LED Carry_Out (.in(nm_alu_fet80_1_c_out));
  nm_regoc8_latch nm_regoc8_latch_1 (.D(Bus), .set(nm_or_5_out), .en(Load_H), .Out(Bus), .V(A[15:8]));
  nm_regoc8_latch nm_regoc8_latch_2 (.D(Bus), .set(nm_or_6_out), .en(Load_L), .Out(Bus), .V(A[7:0]));
  nm_conditionals nm_conditionals_1 (
    .eqz(nm_conditionals_1_eqz), .gtz(nm_conditionals_1_gtz), .ltz(nm_conditionals_1_ltz),
    .nez(nm_conditionals_1_nez), .lez(nm_conditionals_1_lez), .gez(nm_conditionals_1_gez),
    .zr(nm_conditionals_prestage_1_zr), .ng(nm_conditionals_prestage_1_ng));
  LED eq_0 (.in(nm_conditionals_1_eqz));
  LED gt_0 (.in(nm_conditionals_1_gtz));
  LED lt_0 (.in(nm_conditionals_1_ltz));
  LED _0 (.in(nm_conditionals_1_nez));
  LED _0_2 (.in(nm_conditionals_1_lez));
  Button Save_ACC (.out(Save_ACC_out));
  LED _0_3 (.in(nm_conditionals_1_gez));
  nm_or nm_or_7 (.Out(nm_or_7_out), .In_1(set_master), .In_2(Save_ACC_out));
  Button Set_M (.out(Set_M_out));
  nm_regoc8_latch nm_regoc8_latch_3 (.D(ALU), .set(nm_or_7_out), .en(Load_ACC), .Out(Bus), .V(ACC));
  RAMAsync #(.AddrBits(16), .Bits(8)) ramasync_1 (.A(A), .D(Bus), .we(Set_M_out), .Q(M));
  nm_enableoc8 nm_enableoc8_3 (.In(M), .en(Load_M), .Out(Bus));

  assign H = A[15:8];
  assign In = {In_7, In_6, In_5, In_4, In_3, In_2, In_1, In_0};
  assign L = A[7:0];

  // Notes on the sheet:
  //   f: default 1
  //   no: default 1
  //   contents of rom_1 (hex, n*v repeats v):
  //   de,ad,be,ef,57001*0,be,ef
endmodule
