// Digital circuit nm_ALU_FET80.dig as structural Verilog
module nm_ALU_FET80 (
  input  [7:0] X,
  input  [7:0] Y,
  input  nx,
  input  ny,
  input  f,
  input  no,
  input  c_in,
  output [7:0] Out,
  output c_out
);

  wire [7:0] nm_adder8_1_and, nm_adder8_1_sum, nm_inverter8_1_out, nm_inverter8_2_out, nm_mux8_1_out;

  nm_inverter8 nm_inverter8_1 (.In(X), .inv(nx), .Out(nm_inverter8_1_out));
  nm_inverter8 nm_inverter8_2 (.In(Y), .inv(ny), .Out(nm_inverter8_2_out));
  nm_adder8 nm_adder8_1 (
    .A(nm_inverter8_1_out), .B(nm_inverter8_2_out), .sum(nm_adder8_1_sum), .c_in(c_in), .c_out(c_out),
    .\and (nm_adder8_1_and));  // open: xor
  nm_mux8 nm_mux8_1 (.A(nm_adder8_1_and), .B(nm_adder8_1_sum), .s(f), .Out(nm_mux8_1_out));
  nm_inverter8 nm_inverter8_3 (.In(nm_mux8_1_out), .inv(no), .Out(Out));
endmodule
