// Digital circuit nm_Xor.dig as structural Verilog
module nm_Xor (
  input  In_1,
  input  In_2,
  output Out
);

  wire nm_not_1_out, nm_not_2_out;

  nm_Not nm_not_1 (.In(In_1), .Out(nm_not_1_out));
  nm_Not nm_not_2 (.In(In_2), .Out(nm_not_2_out));
  nm_AOI2_2 nm_aoi2_2_1 (.In_1(In_2), .In_2(In_1), .In_3(nm_not_1_out), .In_4(nm_not_2_out), .Out(Out));
endmodule

/* Test case:
In_1 In_2 Out

0 0 0
0 1 1
1 0 1
1 1 0
*/
