// Digital circuit nm_dff_asyncn.dig as structural Verilog
module nm_dff_asyncn (
  input  D,
  input  clk,
  input  r,
  input  s,
  output Q,
  output Q_2
);

  wire nm_srn2_2_1_p2, nm_srn2_2_1_p5, nm_srn2_2_2_p5;

  // nm_srn2_2 nm_srn2_2_1: pin names not known; wires that end beside it: s, nm_srn2_2_1_p2, clk, r, nm_srn2_2_1_p5
  // nm_srn2_2 nm_srn2_2_2: pin names not known; wires that end beside it: nm_srn2_2_1_p5, clk, D, r, nm_srn2_2_2_p5, nm_srn2_2_1_p2
  // nm_srn2_2 nm_srn2_2_3: pin names not known; wires that end beside it: s, nm_srn2_2_1_p5, nm_srn2_2_2_p5, r, Q, Q_2
endmodule
