// Digital circuit nm_dff_resetn.dig as structural Verilog
module nm_dff_resetn (
  input  D,
  input  clk,
  input  r,
  output Q,
  output Q_2
);

  wire nm_not_1_out;

  nm_not nm_not_1 (.In(D), .Out(nm_not_1_out));
  nm_jk_resetn nm_jk_resetn_1 (.J(D), .clk(clk), .r(r), .K(nm_not_1_out), .Q(Q), .Q_2(Q_2));
endmodule
