// Digital circuit nm_enable.dig as structural Verilog
module nm_enable (
  input  In,
  input  en,
  output Out
);

  wire nm_not_1_out;

  nm_not nm_not_1 (.In(In), .Out(nm_not_1_out));
  nm_enablen nm_enablen_1 (.In(nm_not_1_out), .en(en), .Out(Out));
endmodule
